// Logisim project Part_II_3.circ as structural Verilog: 1 circuit, main circuit main
module main (
  input  a,
  input  b,
  input  c,
  input  d,
  output out_5
);

  wire n7404_1_p2, n7404_1_p4, n7408_1_p3, n7408_1_p4, n7408_1_p10;

  // _7404 7404_1: pin names not known; wires that end beside it: b, n7404_1_p2, c, n7404_1_p4, 1'b0, 1'b1
  // _7408 7408_1: pin names not known; wires that end beside it: a, n7404_1_p4, n7408_1_p3, n7408_1_p4, n7408_1_p4, 1'b0, 1'b1, n7404_1_p2, d, n7408_1_p10
  // _7432 7432_1: pin names not known; wires that end beside it: n7408_1_p3, n7408_1_p10, out_5, 1'b0, 1'b1
endmodule
