// Logisim project Part_II_6.circ as structural Verilog: 1 circuit, main circuit main
module main (
  input  a,
  input  b,
  input  c,
  input  d,
  output out_5
);

  wire n7404_1_p2, n7404_1_p4, n7404_1_p7, n7404_1_p8, n7404_1_p9, n7404_1_p11, n7404_1_p12;

  // _7404 7404_1: pin names not known; wires that end beside it: b, n7404_1_p2, c, n7404_1_p4, 1'b0, 1'b1, n7404_1_p7, n7404_1_p8, n7404_1_p9, out_5, n7404_1_p11, n7404_1_p12
  // _7408 7408_1: pin names not known; wires that end beside it: a, n7404_1_p4, n7404_1_p7, n7404_1_p2, d, n7404_1_p11, 1'b0, 1'b1, n7404_1_p8, n7404_1_p12, n7404_1_p9
endmodule
