// Logisim project Part_I_4.circ as structural Verilog: 1 circuit, main circuit main
module main (
  input  x,
  input  y,
  input  s,
  output s_2
);

  wire n7404_1_p1, n7404_1_p4, n7404_1_p7, n7404_1_p8, n7404_1_p9, n7404_1_p10;

  // _7404 7404_1: pin names not known; wires that end beside it: n7404_1_p1, s_2, s, n7404_1_p4, 1'b0, 1'b1, n7404_1_p7, n7404_1_p8, n7404_1_p9, n7404_1_p10
  // _7408 7408_1: pin names not known; wires that end beside it: n7404_1_p4, x, n7404_1_p7, s, y, n7404_1_p9, 1'b0, 1'b1, n7404_1_p8, n7404_1_p10, n7404_1_p1

  // Notes on the sheet:
  //   s_2: pull=up
endmodule
